// Logisim project data path.circ as structural Verilog
module data_path (
  input  in_1,
  input  in_2,
  input  in_3,
  input  [1:0] in_4,
  input  in_5,
  input  in_6,
  input  in_7,
  input  [1:0] in_8,
  input  in_9,
  input  in_10,
  input  in_11,
  input  in_12,
  input  in_13
);

  wire clock_1_out, not_1_out;
  wire [7:0] AC_q, adder_1_out, AR_q, MAR_q, MBR_q, multiplexer_1_out, multiplexer_2_out, multiplexer_3_out,
       PC_q, ram_1_data;

  RAM ram_1 (.addr(MAR_q), .data(ram_1_data), .sel(in_13), .clk(clock_1_out), .ld(in_12));  // open: clr
  Clock clock_1 (.out(clock_1_out));
  Multiplexer #(.width(8), .enable("false")) multiplexer_1 (
    .in0(adder_1_out), .in1(ram_1_data), .out(multiplexer_1_out), .sel(in_7));
  not not_1 (not_1_out, in_12);
  assign ram_1_data = not_1_out ? MBR_q : 8'bz;  // Controlled_Buffer controlled_buffer_1
  Register AC (.D(adder_1_out), .en(in_1), .Q(AC_q), .clk(clock_1_out), .clr(in_11));
  Register PC (.D(adder_1_out), .en(in_2), .Q(PC_q), .clk(clock_1_out), .clr(in_11));
  Register AR (.D(adder_1_out), .en(in_5), .Q(AR_q), .clk(clock_1_out), .clr(in_11));
  Register MBR (.D(multiplexer_1_out), .en(in_6), .Q(MBR_q), .clk(clock_1_out), .clr(in_11));
  Register MAR (.D(adder_1_out), .en(in_9), .Q(MAR_q), .clk(clock_1_out), .clr(in_11));
  Register IR (.D(adder_1_out), .en(in_10), .clk(clock_1_out), .clr(in_11));  // open: Q
  Multiplexer #(.select(2), .width(8), .enable("false")) multiplexer_2 (
    .in0(AC_q), .in1(PC_q), .in2(AR_q), .in3(MBR_q), .out(multiplexer_2_out), .sel(in_4));
  Multiplexer #(.select(2), .width(8), .enable("false")) multiplexer_3 (
    .in0(AC_q), .in1(PC_q), .in2(AR_q), .in3(MBR_q), .out(multiplexer_3_out), .sel(in_8));
  Hex_Digit_Display hex_digit_display_1 (.value(adder_1_out[7:4]));  // open: dp
  Adder adder_1 (.a(multiplexer_2_out), .b(multiplexer_3_out), .out(adder_1_out), .cin(in_3));  // open: cout
  Hex_Digit_Display hex_digit_display_2 (.value(adder_1_out[3:0]));  // open: dp
endmodule
