// Logisim project first_logsim.circ as structural Verilog
// HA
module half_adder (
  input  A,
  input  B,
  output S,
  output C
);

  and and_1 (C, A, B);
  xor xor_1 (S, A, B);

  // Notes on the sheet:
  //   한글도 되나...
endmodule

// FA
module full_adder (
  input  A,
  input  B,
  input  Cin,
  output S,
  output Cout
);

  wire half_adder_1_c, half_adder_1_s, half_adder_2_c;

  half_adder half_adder_1 (.A(A), .B(B), .S(half_adder_1_s), .C(half_adder_1_c));
  half_adder half_adder_2 (.A(half_adder_1_s), .B(Cin), .S(S), .C(half_adder_2_c));
  or or_1 (Cout, half_adder_2_c, half_adder_1_c);
endmodule

module _1x2_Mux (
  input  in_0,
  input  in_1,
  input  select,
  output out
);

  wire and_1_out, and_2_out, not_1_out;

  not not_1 (not_1_out, select);
  and and_1 (and_1_out, in_0, not_1_out);
  and and_2 (and_2_out, in_1, select);
  or or_1 (out, and_1_out, and_2_out);
endmodule

module _2x4_Mux (
  input  in_00,
  input  in_01,
  input  in_10,
  input  in_11,
  input  sel_0,
  input  sel_1,
  output out
);

  wire n1x2_mux_1_out, n1x2_mux_2_out;

  _1x2_Mux u_1x2_mux_1 (.in_0(in_00), .in_1(in_01), .select(sel_1), .out(n1x2_mux_1_out));
  _1x2_Mux u_1x2_mux_2 (.in_0(in_10), .in_1(in_11), .select(sel_1), .out(n1x2_mux_2_out));
  _1x2_Mux u_1x2_mux_3 (.in_0(n1x2_mux_1_out), .in_1(n1x2_mux_2_out), .select(sel_0), .out(out));
endmodule

module _4bit_adder (
  input  Cin,
  input  [3:0] in_2,
  input  [3:0] in_3,
  output [3:0] out_4,
  output Cout
);

  wire full_adder_1_cout, full_adder_2_cout, full_adder_3_cout;

  full_adder full_adder_1 (.A(in_2[0]), .B(in_3[0]), .Cin(Cin), .S(out_4[0]), .Cout(full_adder_1_cout));
  full_adder full_adder_2 (.A(in_2[1]), .B(in_3[1]), .Cin(full_adder_1_cout), .S(out_4[1]), .Cout(full_adder_2_cout));
  full_adder full_adder_3 (.A(in_2[2]), .B(in_3[2]), .Cin(full_adder_2_cout), .S(out_4[2]), .Cout(full_adder_3_cout));
  full_adder full_adder_4 (.A(in_2[3]), .B(in_3[3]), .Cin(full_adder_3_cout), .S(out_4[3]), .Cout(Cout));
endmodule
